# Fritzing sketch pi-clock (saved by Fritzing 0.9.3b)
breadboards: 1

parts:
  Raspberry_Pi1 = Raspberry Pi 2
  LED1 = 7-SEGMENT-4DIGIT-YOUNGSUN [package=7-segment-4digit-youngsun-longpads]
  R1 = Resistor [tolerance=±5% resistance=220 package=THT]
  R2 = Resistor [tolerance=±5% resistance=220 package=THT]
  R3 = Resistor [tolerance=±5% resistance=220 package=THT]
  R4 = Resistor [tolerance=±5% resistance=220 package=THT]
  R5 = Resistor [tolerance=±5% resistance=220 package=THT]
  R6 = Resistor [tolerance=±5% resistance=220 package=THT]
  R7 = Resistor [tolerance=±5% resistance=220 package=THT]
  R8 = Resistor [tolerance=±5% resistance=220 package=THT]

nets:
  N1: Raspberry_Pi1.GPIO2, LED1.APOS-A, R2.Pin_0
  N2: Raspberry_Pi1.GPIO3, LED1.F
  N3: Raspberry_Pi1.GPIO17, R5.Pin_0
  N4: Raspberry_Pi1.GPIO27, R4.Pin_0
  N5: Raspberry_Pi1.GPIO22, R6.Pin_1
  N6: Raspberry_Pi1.GPIO10, R2.Pin_1
  N7: Raspberry_Pi1.GPIO8, R3.Pin_0
  N8: Raspberry_Pi1.GPIO25, R1.Pin_1
  N9: Raspberry_Pi1.GPIO24, R8.Pin_1
  N10: Raspberry_Pi1.GPIO23, R7.Pin_1
  N11: Raspberry_Pi1.GPIO15, LED1.G
  N12: Raspberry_Pi1.GPIO14, LED1.DP
  N13: LED1.DIG2, R5.Pin_1
  N14: LED1.D, R4.Pin_1
  N15: LED1.COL-A, R6.Pin_0
  N16: LED1.E, R7.Pin_0
  N17: LED1.DIG3, R8.Pin_0
  N18: LED1.C, R1.Pin_0
  N19: LED1.A, R3.Pin_1
